// Logisim project exp4-2.circ as structural Verilog: 4 circuits, main circuit main
module main (
  output Cin,
  output [15:0] X,
  output halt,
  output [15:0] Y,
  output Cout,
  output [15:0] S
);

  wire [3:0] bit_extender_1_out, counter_1_q;

  Clock clock_1 (.out(Cin));
  Counter #(.width(4), .max('hf), .trigger("falling")) counter_1 (
    .Q(counter_1_q), .carry(halt), .clk(Cin));  // open: load, D, count, clr, preset, down
  assign bit_extender_1_out = {{3{1'b0}}, Cin};  // Bit_Extender bit_extender_1
  ROM #(.addrWidth(4), .dataWidth(16), .Select("low")) \X取值  (.addr(counter_1_q), .data(X));
  ROM #(.addrWidth(4), .dataWidth(16), .Select("low")) \Y取值  (.addr(counter_1_q), .data(Y));
  Hex_Digit_Display hex_digit_display_1 (.value(bit_extender_1_out));  // open: dp
  Hex_Digit_Display hex_digit_display_2 (.value(S[15:12]));  // open: dp
  Hex_Digit_Display hex_digit_display_3 (.value(X[11:8]));  // open: dp
  Hex_Digit_Display hex_digit_display_4 (.value(X[15:12]));  // open: dp
  Hex_Digit_Display hex_digit_display_5 (.value(S[11:8]));  // open: dp
  Hex_Digit_Display hex_digit_display_6 (.value(S[7:4]));  // open: dp
  Hex_Digit_Display hex_digit_display_7 (.value(X[3:0]));  // open: dp
  Hex_Digit_Display hex_digit_display_8 (.value(X[7:4]));  // open: dp
  Hex_Digit_Display hex_digit_display_9 (.value(S[3:0]));  // open: dp
  \_16位CLA  \u_16位cla_1  (
    .Cin(Cin), .X1(X[3:0]), .Y1(Y[3:0]), .X2(X[7:4]), .Y2(Y[7:4]), .X3(X[11:8]), .Y3(Y[11:8]), .X4(X[15:12]),
    .Y4(Y[15:12]), .S1(S[3:0]), .S2(S[7:4]), .S3(S[11:8]), .S4(S[15:12]), .Cout(Cout));
  Hex_Digit_Display hex_digit_display_10 (.value(Y[15:12]));  // open: dp
  LED led_1 (.in(Cout));
  Hex_Digit_Display hex_digit_display_11 (.value(Y[7:4]));  // open: dp
  Hex_Digit_Display hex_digit_display_12 (.value(Y[11:8]));  // open: dp
  Hex_Digit_Display hex_digit_display_13 (.value(Y[3:0]));  // open: dp

  // Notes on the sheet:
  //   =
  //   contents of X取值 (hex, n*v repeats v):
  //   0 1111 2222 3333 4444 5555 6666 7777 8888 9999 a00a b00b c00c d00d eeee ffff
  //   contents of Y取值 (hex, n*v repeats v):
  //   aaaa ffff 101 202 303 a0a b0b c0c d0d f0f eeee dddd cccc bbbb 1 1
  //   Cin
  //   +
  //   S1
  //   X1
  //   X1
  //   S3
  //   S2
  //   顶层模块与自制子模块连接部分
  //   本地Logisim验证区域
  //   按Control+K触发执行，再次按Control+K暂停触发
  //   X1
  //   X1
  //   S4
  //   +
  //   Y1
  //   Cout
  //   Y3
  //   Y2
  //   Y4
endmodule

// 组间进位函数逻辑
module \组间进位函数逻辑单元  (
  input  P1,
  input  G1,
  input  P2,
  input  G2,
  input  P3,
  input  G3,
  input  P4,
  input  G4,
  output Pg,
  output Gg
);

  wire and_1_out, and_3_out, and_4_out;

  and and_1 (and_1_out, P4, G3);
  and and_2 (Gg, P1, P2, P3, P4);
  and and_3 (and_3_out, G1, P2, P3, P4);
  and and_4 (and_4_out, G2, P3, P4);
  or or_1 (Pg, and_3_out, and_4_out, and_1_out, G4);

  // Notes on the sheet:
  //   组间进位函数逻辑单元子模块实现区域
endmodule

// 4-bit CLA
module \可级联的4位CLA  (
  input  Cin,
  input  [3:0] X,
  input  [3:0] Y,
  output Pg,
  output Gg,
  output [3:0] S,
  output Cout
);

  wire and_1_out, and_2_out, and_3_out, and_4_out, or_1_out, or_2_out, or_3_out, or_4_out;

  or or_1 (or_1_out, X[0], Y[0]);
  and and_1 (and_1_out, X[0], Y[0]);
  or or_2 (or_2_out, X[1], Y[1]);
  and and_2 (and_2_out, X[1], Y[1]);
  or or_3 (or_3_out, X[2], Y[2]);
  and and_3 (and_3_out, X[2], Y[2]);
  or or_4 (or_4_out, X[3], Y[3]);
  and and_4 (and_4_out, X[3], Y[3]);
  \_4位CLA  \u_4位cla_1  (
    .X1(X[0]), .S1(S[0]), .S2(S[1]), .S3(S[2]), .S4(S[3]), .Y1(Y[0]), .X2(X[1]), .Y2(Y[1]), .X3(X[2]),
    .Y3(Y[2]), .X4(X[3]), .Y4(Y[3]), .Cin(Cin), .Cout(Cout));
  \组间进位函数逻辑单元  \u_组间进位函数逻辑单元_1  (
    .P1(or_1_out), .G1(and_1_out), .P2(or_2_out), .G2(and_2_out), .P3(or_3_out), .G3(and_3_out),
    .P4(or_4_out), .G4(and_4_out), .Pg(Pg), .Gg(Gg));

  // Notes on the sheet:
  //   先行进位加法器子模块实现区域
endmodule

// 16-bit CLA
module \_16位CLA  (
  input  Cin,
  input  [3:0] X1,
  input  [3:0] Y1,
  input  [3:0] X2,
  input  [3:0] Y2,
  input  [3:0] X3,
  input  [3:0] Y3,
  input  [3:0] X4,
  input  [3:0] Y4,
  output [3:0] S1,
  output [3:0] S2,
  output [3:0] S3,
  output [3:0] S4,
  output Cout
);

  wire \n4位clu_1_c1 , \n4位clu_1_c2 , \n4位clu_1_c3 , \可级联的4位cla_1_gg , \可级联的4位cla_1_pg , \可级联的4位cla_2_gg ,
       \可级联的4位cla_2_pg , \可级联的4位cla_3_gg , \可级联的4位cla_3_pg , \可级联的4位cla_4_gg , \可级联的4位cla_4_pg ;

  \可级联的4位CLA  \u_可级联的4位cla_1  (
    .X(X1), .S(S1), .Y(Y1), .Cin(Cin), .Pg(\可级联的4位cla_1_pg ), .Gg(\可级联的4位cla_1_gg ));  // open: Cout
  \可级联的4位CLA  \u_可级联的4位cla_2  (
    .X(X2), .S(S2), .Y(Y2), .Cin(\n4位clu_1_c1 ), .Pg(\可级联的4位cla_2_pg ), .Gg(\可级联的4位cla_2_gg ));  // open: Cout
  \可级联的4位CLA  \u_可级联的4位cla_3  (
    .X(X3), .S(S3), .Y(Y3), .Cin(\n4位clu_1_c2 ), .Pg(\可级联的4位cla_3_pg ), .Gg(\可级联的4位cla_3_gg ));  // open: Cout
  \可级联的4位CLA  \u_可级联的4位cla_4  (
    .X(X4), .S(S4), .Y(Y4), .Cin(\n4位clu_1_c3 ), .Cout(Cout), .Pg(\可级联的4位cla_4_pg ), .Gg(\可级联的4位cla_4_gg ));
  \_4位CLU  \u_4位clu_1  (
    .P1(\可级联的4位cla_1_pg ), .C1(\n4位clu_1_c1 ), .C2(\n4位clu_1_c2 ), .G1(\可级联的4位cla_1_gg ),
    .P2(\可级联的4位cla_2_pg ), .G2(\可级联的4位cla_2_gg ), .P3(\可级联的4位cla_3_pg ), .G3(\可级联的4位cla_3_gg ),
    .P4(\可级联的4位cla_4_pg ), .G4(\可级联的4位cla_4_gg ), .C0(Cin), .C3(\n4位clu_1_c3 ));  // open: C4

  // Notes on the sheet:
  //   16位级联先行进位加法器子模块实现区域
endmodule
