// Logisim project exp4-3.circ as structural Verilog: 4 circuits, main circuit main
module main (
  output [3:0] ALUctr,
  output [3:0] X,
  output [3:0] Y,
  output Zero,
  output [3:0] Result,
  output halt
);

  wire clk, comparator_1_eq, not_1_out;
  wire [3:0] counter_1_q, counter_2_q, rom_1_data;

  Clock clock_1 (.out(clk));
  Counter #(.width(4), .max('hf), .trigger("falling")) counter_1 (
    .Q(counter_1_q), .carry(halt), .clk(clk));  // open: load, D, count, clr, preset, down
  // Probe on ALUctr
  Hex_Digit_Display hex_digit_display_1 (.value(X));  // open: dp
  Hex_Digit_Display hex_digit_display_2 (.value(Y));  // open: dp
  ROM #(.addrWidth(4), .dataWidth(4), .Select("low")) \ALUctr取值  (.addr(counter_1_q), .data(ALUctr));
  ROM #(.addrWidth(4), .dataWidth(4), .Select("low")) \X取值  (.addr(counter_1_q), .data(X));
  ROM #(.addrWidth(4), .dataWidth(4), .Select("low")) \Y取值  (.addr(counter_1_q), .data(Y));
  Hex_Digit_Display hex_digit_display_3 (.value(Result));  // open: dp
  LED led_1 (.in(Zero));
  Counter #(.width(4), .max('hf), .trigger("falling")) counter_2 (
    .Q(counter_2_q), .clk(clk));  // open: load, D, count, carry, clr, preset, down
  \算术逻辑部件_ALU  \u_算术逻辑部件_alu_1  (.X(X), .Y(Y), .ALUctr(ALUctr), .Zero(Zero), .Result(Result));
  ROM #(.addrWidth(4), .dataWidth(4), .Select("low")) rom_1 (.addr(counter_2_q), .data(rom_1_data));
  Comparator #(.width(4), .mode("unsigned")) comparator_1 (
    .a(rom_1_data), .b(Result), .eq(comparator_1_eq));  // open: gt, lt
  not not_1 (not_1_out, comparator_1_eq);
  RAM #(.addrWidth(4), .dataWidth(16), .bus("separate"), .Select("low")) \ALU指令执行错误记录  (
    .addr(counter_2_q), .din({counter_2_q, ALUctr, X, Y}), .str(not_1_out), .clk(clk));  // open: data, sel, ld, clr

  // Notes on the sheet:
  //   ALUctr
  //   操作数X
  //   操作数Y
  //   contents of ALUctr取值 (hex, n*v repeats v):
  //   0 0 0 2 2 2 3 3 3 6 6 6 8 8 8 f
  //   contents of X取值 (hex, n*v repeats v):
  //   1 a f 3 3 0 3 3 a f 0 a f 3 1 3
  //   contents of Y取值 (hex, n*v repeats v):
  //   2 a 1 7 8 a 7 8 8 0 5 9 1 3 3 5
  //   Result
  //   Zero
  //   顶层模块与自制子模块连接部分
  //   本地Logisim验证区域
  //   按Control+K触发执行，再次按Control+K暂停触发
  //   错误记录
  //   contents of rom_1 (hex, n*v repeats v):
  //   3 4 0 1 0 0 1 1 0 f 5 b e 0 e 5
  //   记录每个条目为16bits：
  //   最高4位为指令index，
  //   次高4位为ALUctr，
  //   次低4位为操作数X，
  //   最低4位为操作数Y。
endmodule

// 4-bit adder
module \_4位带标志位加法器  (
  input  Cin,
  input  X1,
  input  Y1,
  input  X2,
  input  Y2,
  input  X3,
  input  Y3,
  input  X4,
  input  Y4,
  output OF,
  output SF,
  output ZF,
  output CF,
  output S1,
  output S2,
  output S3,
  output S4
);

  wire adder_1_cout, adder_2_cout, adder_3_cout, adder_4_cout;

  Adder #(.width(1)) adder_1 (.a(X1), .b(Y1), .out(S1), .cin(Cin), .cout(adder_1_cout));
  Adder #(.width(1)) adder_2 (.a(X2), .b(Y2), .out(S2), .cin(adder_1_cout), .cout(adder_2_cout));
  Adder #(.width(1)) adder_3 (.a(X3), .b(Y3), .out(S3), .cin(adder_2_cout), .cout(adder_3_cout));
  Adder #(.width(1)) adder_4 (.a(X4), .b(Y4), .out(S4), .cin(adder_3_cout), .cout(adder_4_cout));
  xor xor_1 (OF, adder_3_cout, adder_4_cout);
  nor nor_1 (ZF, S1, S2, S3, S4);
  xor xor_2 (CF, Cin, adder_4_cout);

  assign SF = S4;

  // Notes on the sheet:
  //   带标志位加法器子模块实现区域
endmodule

module \ALU操作控制信号生成部件  (
  input  [3:0] ALUctr,
  output SUBctr,
  output SIGctr,
  output OPctr0,
  output OPctr1
);

  wire and_1_out, and_2_out, and_3_out, not_3_out, not_4_out;

  not not_1 (SIGctr, ALUctr[0]);
  // NOT_Gate not_2 has open pins: in=ALUctr[1], out=open
  not not_3 (not_3_out, ALUctr[2]);
  not not_4 (not_4_out, ALUctr[3]);
  and and_1 (and_1_out, ALUctr[1], not_3_out, not_4_out);
  and and_2 (and_2_out, SIGctr, ALUctr[1], ALUctr[2], not_4_out);
  and and_3 (and_3_out, ALUctr[0], ALUctr[1], ALUctr[2], ALUctr[3]);
  or or_1 (SUBctr, ALUctr[3], and_1_out);
  or or_2 (OPctr0, and_1_out, and_2_out);
  or or_3 (OPctr1, and_1_out, and_3_out);

  // Notes on the sheet:
  //   ALU操作控制信号生成子模块实现区域
endmodule

// ALU
module \算术逻辑部件_ALU  (
  input  [3:0] X,
  input  [3:0] Y,
  input  [3:0] ALUctr,
  output Zero,
  output [3:0] Result
);

  wire \alu操作控制信号生成部件_1_sigctr , \alu操作控制信号生成部件_1_subctr , multiplexer_2_out, \n4位带标志位加法器_1_cf ,
       \n4位带标志位加法器_1_of , \n4位带标志位加法器_1_sf , xor_2_out, xor_3_out;
  wire [1:0] \alu操作控制信号生成部件_1_opctr0 ;
  wire [3:0] bit_extender_1_out, bit_extender_2_out, \n4位带标志位加法器_1_s1 , or_1_out, xor_1_out;

  assign bit_extender_1_out = {{3{\alu操作控制信号生成部件_1_subctr }}, \alu操作控制信号生成部件_1_subctr };  // Bit_Extender bit_extender_1
  assign xor_1_out = Y ^ bit_extender_1_out;  // XOR_Gate xor_1, 4 bits wide
  assign or_1_out = X | Y;  // OR_Gate or_1, 4 bits wide
  \_4位带标志位加法器  \u_4位带标志位加法器_1  (
    .X1(X[0]), .S1(\n4位带标志位加法器_1_s1 [0]), .S2(\n4位带标志位加法器_1_s1 [1]), .S3(\n4位带标志位加法器_1_s1 [2]),
    .S4(\n4位带标志位加法器_1_s1 [3]), .Y1(xor_1_out[0]), .X2(X[1]), .Y2(xor_1_out[1]), .X3(X[2]), .Y3(xor_1_out[2]),
    .X4(X[3]), .Y4(xor_1_out[3]), .Cin(\alu操作控制信号生成部件_1_subctr ), .SF(\n4位带标志位加法器_1_sf ), .ZF(Zero),
    .CF(\n4位带标志位加法器_1_cf ), .OF(\n4位带标志位加法器_1_of ));
  Multiplexer #(.select(2), .width(4), .enable("false")) multiplexer_1 (
    .in0(\n4位带标志位加法器_1_s1 ), .in1(or_1_out), .in2(Y), .in3(bit_extender_2_out), .out(Result),
    .sel(\alu操作控制信号生成部件_1_opctr0 ));
  xor xor_2 (xor_2_out, ~\alu操作控制信号生成部件_1_subctr , \n4位带标志位加法器_1_cf );  // XOR_Gate
  Multiplexer #(.enable("false")) multiplexer_2 (
    .in0(xor_2_out), .in1(xor_3_out), .out(multiplexer_2_out), .sel(\alu操作控制信号生成部件_1_sigctr ));
  xor xor_3 (xor_3_out, \n4位带标志位加法器_1_sf , \n4位带标志位加法器_1_of );
  \ALU操作控制信号生成部件  \alu操作控制信号生成部件_1  (
    .ALUctr(ALUctr), .SUBctr(\alu操作控制信号生成部件_1_subctr ), .SIGctr(\alu操作控制信号生成部件_1_sigctr ),
    .OPctr0(\alu操作控制信号生成部件_1_opctr0 [0]), .OPctr1(\alu操作控制信号生成部件_1_opctr0 [1]));
  assign bit_extender_2_out = {{3{1'b0}}, multiplexer_2_out};  // Bit_Extender bit_extender_2

  // Notes on the sheet:
  //   算术逻辑部件子模块实现区域
endmodule
