// Logisim project exp1-1.circ as structural Verilog: 4 circuits, main circuit main
module main (
  output A,
  output B,
  output Y,
  output halt
);

  wire clock_1_out;

  Counter #(.width(2), .max('h3), .behavior("old")) counter_1 (
    .Q({B, A}), .carry(halt), .clk(clock_1_out));  // open: load, D, count, clr, preset
  Clock clock_1 (.out(clock_1_out));
  \or  or_1 (.A(A), .B(B), .Y(Y));
  LED led_1 (.in(Y));

  // Notes on the sheet:
  //   顶层模块与自制子模块连接部分
  //   本地Logisim验证区域
  //   按Control+K触发执行，再次按Control+K暂停触发
endmodule

module \or  (
  input  A,
  input  B,
  output Y
);

  wire nor_1_y;

  \nor  nor_1 (.A(A), .B(B), .Y(nor_1_y));
  \not  not_1 (.A(nor_1_y), .Y(Y));

  // Notes on the sheet:
  //   自制子模块实现区域
endmodule

// NOR
module \nor  (
  input  A,
  input  B,
  output Y
);

  wire transistor_1_out;

  Transistor transistor_1 (.in(1'b1), .out(transistor_1_out), .gate(A));
  Transistor transistor_2 (.in(transistor_1_out), .out(Y), .gate(B));
  Transistor #(.\type ("n")) transistor_3 (.in(1'b0), .out(Y), .gate(A));
  Transistor #(.\type ("n")) transistor_4 (.in(1'b0), .out(Y), .gate(B));

  // Notes on the sheet:
  //   NOR
endmodule

module \not  (
  input  A,
  output Y
);

  Transistor transistor_1 (.in(1'b1), .out(Y), .gate(A));
  Transistor #(.\type ("n")) transistor_2 (.in(1'b0), .out(Y), .gate(A));

  // Notes on the sheet:
  //   NOR
endmodule
