// Logisim project exp4-1+先行进位加法器+-+作答区.circ as structural Verilog: 4 circuits, main circuit main
module main (
  output Cin,
  output [3:0] X,
  output [3:0] Y,
  output [3:0] S,
  output Cout,
  output halt
);

  wire [3:0] bit_extender_1_out, counter_1_q;

  Clock clock_1 (.out(Cin));
  Counter #(.width(4), .max('hf)) counter_1 (
    .Q(counter_1_q), .carry(halt), .clk(Cin));  // open: load, D, count, clr, preset, down
  assign bit_extender_1_out = {{3{1'b0}}, Cin};  // Bit_Extender bit_extender_1
  Hex_Digit_Display hex_digit_display_1 (.value(bit_extender_1_out));  // open: dp
  ROM #(.addrWidth(4), .dataWidth(4), .Select("low")) \X取值  (.addr(counter_1_q), .data(Y));
  ROM #(.addrWidth(4), .dataWidth(4), .Select("low")) \Y取值  (.addr(counter_1_q), .data(X));
  Hex_Digit_Display hex_digit_display_2 (.value(X));  // open: dp
  Hex_Digit_Display hex_digit_display_3 (.value(Y));  // open: dp
  Hex_Digit_Display hex_digit_display_4 (.value(S));  // open: dp
  \_4位CLA  \u_4位cla_1  (
    .X1(Y[0]), .S1(S[0]), .S2(S[1]), .S3(S[2]), .S4(S[3]), .Y1(X[0]), .X2(Y[1]), .Y2(X[1]), .X3(Y[2]),
    .Y3(X[2]), .X4(Y[3]), .Y4(X[3]), .Cin(Cin), .Cout(Cout));
  LED led_1 (.in(Cout));

  // Notes on the sheet:
  //   Cin
  //   contents of X取值 (hex, n*v repeats v):
  //   0 1 2 3 4 5 6 7 8 9 a b c d e f
  //   contents of Y取值 (hex, n*v repeats v):
  //   a 0 1 2 3 a b c d f e d c 0 1 1
  //   +
  //   X
  //   +
  //   顶层模块与自制子模块连接部分
  //   本地Logisim验证区域
  //   按Control+K触发执行，再次按Control+K暂停触发
  //   Y
  //   =
  //   S
  //   Cout
endmodule

// FA
module \_1位全加器  (
  input  Cin,
  input  A,
  input  B,
  output F,
  output P,
  output G
);


  // Notes on the sheet:
  //   全加法器子模块实现区域
endmodule

// 4-bit CLU
module \_4位CLU  (
  input  C0,
  input  P1,
  input  G1,
  input  P2,
  input  G2,
  input  P3,
  input  G3,
  input  P4,
  input  G4,
  output C1,
  output C2,
  output C3,
  output C4
);


  // Notes on the sheet:
  //   先行进位逻辑单元子模块实现区域
endmodule

// 4-bit CLA
module \_4位CLA  (
  input  Cin,
  input  X1,
  input  Y1,
  input  X2,
  input  Y2,
  input  X3,
  input  Y3,
  input  X4,
  input  Y4,
  output S1,
  output S2,
  output S3,
  output S4,
  output Cout
);


  // Notes on the sheet:
  //   先行进位加法器子模块实现区域
endmodule
