// Logisim project exp4-3+算术逻辑部件+-+作答区.circ as structural Verilog: 4 circuits, main circuit main
module main (
  output [3:0] ALUctr,
  output [3:0] X,
  output [3:0] Y,
  output Zero,
  output [3:0] Result,
  output halt
);

  wire clk, comparator_1_eq, not_1_out;
  wire [3:0] counter_1_q, counter_2_q, rom_1_data;

  Clock clock_1 (.out(clk));
  Counter #(.width(4), .max('hf), .trigger("falling")) counter_1 (
    .Q(counter_1_q), .carry(halt), .clk(clk));  // open: load, D, count, clr, preset, down
  // Probe on ALUctr
  Hex_Digit_Display hex_digit_display_1 (.value(X));  // open: dp
  Hex_Digit_Display hex_digit_display_2 (.value(Y));  // open: dp
  ROM #(.addrWidth(4), .dataWidth(4), .Select("low")) \ALUctr取值  (.addr(counter_1_q), .data(ALUctr));
  ROM #(.addrWidth(4), .dataWidth(4), .Select("low")) \X取值  (.addr(counter_1_q), .data(X));
  ROM #(.addrWidth(4), .dataWidth(4), .Select("low")) \Y取值  (.addr(counter_1_q), .data(Y));
  Hex_Digit_Display hex_digit_display_3 (.value(Result));  // open: dp
  LED led_1 (.in(Zero));
  Counter #(.width(4), .max('hf), .trigger("falling")) counter_2 (
    .Q(counter_2_q), .clk(clk));  // open: load, D, count, carry, clr, preset, down
  \算术逻辑部件_ALU  \u_算术逻辑部件_alu_1  (.X(X), .Y(Y), .ALUctr(ALUctr), .Zero(Zero), .Result(Result));
  ROM #(.addrWidth(4), .dataWidth(4), .Select("low")) rom_1 (.addr(counter_2_q), .data(rom_1_data));
  Comparator #(.width(4), .mode("unsigned")) comparator_1 (
    .a(rom_1_data), .b(Result), .eq(comparator_1_eq));  // open: gt, lt
  not not_1 (not_1_out, comparator_1_eq);
  RAM #(.addrWidth(4), .dataWidth(16), .bus("separate"), .Select("low")) \ALU指令执行错误记录  (
    .addr(counter_2_q), .din({counter_2_q, ALUctr, X, Y}), .str(not_1_out), .clk(clk));  // open: data, sel, ld, clr

  // Notes on the sheet:
  //   ALUctr
  //   操作数X
  //   操作数Y
  //   contents of ALUctr取值 (hex, n*v repeats v):
  //   0 0 0 2 2 2 3 3 3 6 6 6 8 8 8 f
  //   contents of X取值 (hex, n*v repeats v):
  //   1 a f 3 3 0 3 3 a f 0 a f 3 1 3
  //   contents of Y取值 (hex, n*v repeats v):
  //   2 a 1 7 8 a 7 8 8 0 5 9 1 3 3 5
  //   Result
  //   Zero
  //   顶层模块与自制子模块连接部分
  //   本地Logisim验证区域
  //   按Control+K触发执行，再次按Control+K暂停触发
  //   错误记录
  //   contents of rom_1 (hex, n*v repeats v):
  //   3 4 0 1 0 0 1 1 0 f 5 b e 0 e 5
  //   记录每个条目为16bits：
  //   最高4位为指令index，
  //   次高4位为ALUctr，
  //   次低4位为操作数X，
  //   最低4位为操作数Y。
endmodule

// 4-bit adder
module \_4位带标志位加法器  (
  input  Cin,
  input  X1,
  input  Y1,
  input  X2,
  input  Y2,
  input  X3,
  input  Y3,
  input  X4,
  input  Y4,
  output OF,
  output SF,
  output ZF,
  output CF,
  output S1,
  output S2,
  output S3,
  output S4
);


  // Notes on the sheet:
  //   带标志位加法器子模块实现区域
endmodule

module \ALU操作控制信号生成部件  (
  input  [3:0] ALUctr,
  output SUBctr,
  output SIGctr,
  output OPctr0,
  output OPctr1
);

  wire and_1_out, and_2_out, and_3_out, not_3_out, not_4_out;

  not not_1 (SIGctr, ALUctr[0]);
  // NOT_Gate not_2 has open pins: in=ALUctr[1], out=open
  not not_3 (not_3_out, ALUctr[2]);
  not not_4 (not_4_out, ALUctr[3]);
  and and_1 (and_1_out, ALUctr[1], not_3_out, not_4_out);
  and and_2 (and_2_out, SIGctr, ALUctr[1], ALUctr[2], not_4_out);
  and and_3 (and_3_out, ALUctr[0], ALUctr[1], ALUctr[2], ALUctr[3]);
  or or_1 (SUBctr, ALUctr[3], and_1_out);
  or or_2 (OPctr0, and_1_out, and_2_out);
  or or_3 (OPctr1, and_1_out, and_3_out);

  // Notes on the sheet:
  //   ALU操作控制信号生成子模块实现区域
endmodule

// ALU
module \算术逻辑部件_ALU  (
  input  [3:0] X,
  input  [3:0] Y,
  input  [3:0] ALUctr,
  output Zero,
  output [3:0] Result
);


  // Notes on the sheet:
  //   算术逻辑部件子模块实现区域
endmodule
