// Logisim project exp5-2 【示例】控制器.circ as structural Verilog: 1 circuit, main circuit 控制器
module \控制器  (
  input  op0,
  input  op1,
  input  op2,
  input  op3,
  input  op4,
  input  op5,
  input  op6,
  input  fn0,
  input  fn1,
  input  fn2,
  output Branch,
  output Jump,
  output MemtoReg,
  output RegWr,
  output MemWr,
  output ALUctr0,
  output ALUctr1,
  output ALUctr2,
  output ALUctr3,
  output ALUASrc,
  output ALUBSrc0,
  output ALUBSrc1,
  output ExtOP0,
  output ExtOP1,
  output ExtOP2
);

  wire and_4_out, and_5_out, and_6_out, and_7_out, and_8_out, and_9_out, and_10_out, and_11_out, and_12_out,
       and_13_out, and_14_out, and_19_out, and_20_out, and_21_out, and_22_out, and_23_out, and_24_out,
       and_25_out, not_1_out, not_2_out, not_3_out, not_4_out, not_5_out, not_6_out, not_7_out, not_8_out,
       not_9_out, not_10_out, not_11_out, not_12_out, not_13_out, not_14_out, not_15_out, not_16_out,
       not_17_out, not_18_out, not_19_out, not_20_out, not_21_out, not_22_out, not_23_out, not_24_out,
       not_25_out, not_26_out, not_27_out, not_28_out, not_29_out, not_30_out, not_31_out, not_32_out,
       not_33_out, not_34_out, not_35_out, not_36_out, not_37_out, not_38_out, not_39_out, not_40_out,
       not_41_out, not_42_out, not_43_out, not_44_out, not_45_out, not_46_out, not_47_out, not_48_out,
       not_49_out, not_50_out, not_51_out, not_52_out, not_53_out, not_54_out, not_55_out, not_56_out,
       not_57_out, not_58_out, not_59_out, not_60_out, not_61_out, not_62_out, not_63_out, not_64_out,
       not_65_out, not_66_out, not_67_out, not_68_out, not_69_out, not_70_out, not_71_out, not_72_out,
       not_73_out, not_74_out, not_75_out, not_76_out, not_77_out, not_78_out;

  not not_1 (not_1_out, op2);
  not not_2 (not_2_out, op3);
  not not_3 (not_3_out, op4);
  not not_4 (not_4_out, op4);
  not not_5 (not_5_out, op2);
  not not_6 (not_6_out, op3);
  not not_7 (not_7_out, op4);
  not not_8 (not_8_out, op5);
  not not_9 (not_9_out, op6);
  not not_10 (not_10_out, op2);
  not not_11 (not_11_out, op3);
  not not_12 (not_12_out, op5);
  not not_13 (not_13_out, op6);
  not not_14 (not_14_out, op3);
  not not_15 (not_15_out, op6);
  not not_16 (not_16_out, op4);
  not not_17 (not_17_out, op2);
  not not_18 (not_18_out, op3);
  not not_19 (not_19_out, op4);
  not not_20 (not_20_out, op6);
  not not_21 (not_21_out, fn0);
  not not_22 (not_22_out, fn2);
  not not_23 (not_23_out, op2);
  not not_24 (not_24_out, op3);
  not not_25 (not_25_out, op6);
  not not_26 (not_26_out, op3);
  not not_27 (not_27_out, op6);
  not not_28 (not_28_out, op2);
  not not_29 (not_29_out, op3);
  not not_30 (not_30_out, op6);
  not not_31 (not_31_out, op3);
  not not_32 (not_32_out, op6);
  not not_33 (not_33_out, op2);
  not not_34 (not_34_out, op3);
  not not_35 (not_35_out, op6);
  not not_36 (not_36_out, op3);
  not not_37 (not_37_out, op6);
  not not_38 (not_38_out, op2);
  not not_39 (not_39_out, op3);
  not not_40 (not_40_out, op4);
  not not_41 (not_41_out, op3);
  not not_42 (not_42_out, op6);
  not not_43 (not_43_out, op4);
  not not_44 (not_44_out, op4);
  not not_45 (not_45_out, op2);
  not not_46 (not_46_out, op3);
  not not_47 (not_47_out, op4);
  not not_48 (not_48_out, op6);
  not not_49 (not_49_out, fn0);
  not not_50 (not_50_out, fn2);
  not not_51 (not_51_out, op2);
  not not_52 (not_52_out, op3);
  not not_53 (not_53_out, op5);
  not not_54 (not_54_out, op6);
  not not_55 (not_55_out, fn0);
  not not_56 (not_56_out, op3);
  not not_57 (not_57_out, op6);
  not not_58 (not_58_out, op2);
  not not_59 (not_59_out, op3);
  not not_60 (not_60_out, op4);
  not not_61 (not_61_out, fn0);
  not not_62 (not_62_out, fn1);
  not not_63 (not_63_out, fn2);
  not not_64 (not_64_out, op3);
  not not_65 (not_65_out, op6);
  not not_66 (not_66_out, op2);
  not not_67 (not_67_out, op3);
  not not_68 (not_68_out, op4);
  not not_69 (not_69_out, op6);
  not not_70 (not_70_out, fn0);
  not not_71 (not_71_out, fn2);
  not not_72 (not_72_out, op2);
  not not_73 (not_73_out, op3);
  not not_74 (not_74_out, op4);
  not not_75 (not_75_out, fn0);
  not not_76 (not_76_out, fn1);
  not not_77 (not_77_out, fn2);
  not not_78 (not_78_out, op4);
  and and_1 (Branch, op0, op1, not_1_out, not_2_out, not_3_out, op5, op6);
  and and_2 (Jump, op0, op1, op2, op3, not_4_out, op5, op6);
  and and_3 (MemtoReg, op0, op1, not_5_out, not_6_out, not_7_out, not_8_out, not_9_out);
  and and_4 (and_4_out, op0, op1, not_10_out, not_11_out, not_12_out, not_13_out);
  and and_5 (and_5_out, op0, op1, not_14_out, op4, op5, not_15_out);
  and and_6 (and_6_out, op0, op1, op2, op3, not_16_out, op5, op6);
  and and_7 (and_7_out, op0, op1, not_23_out, not_24_out, op4, not_25_out, fn0);
  and and_8 (and_8_out, op0, op1, op2, not_26_out, op4, op5, not_27_out);
  and and_9 (and_9_out, op0, op1, not_28_out, not_29_out, op4, not_30_out, fn1);
  and and_10 (and_10_out, op0, op1, op2, not_31_out, op4, op5, not_32_out);
  and and_11 (and_11_out, op0, op1, not_33_out, not_34_out, op4, not_35_out, fn2);
  and and_12 (and_12_out, op0, op1, op2, not_36_out, op4, op5, not_37_out);
  and and_13 (and_13_out, op0, op1, not_38_out, not_39_out, not_40_out, op5, op6);
  and and_14 (and_14_out, op0, op1, op2, not_41_out, op4, op5, not_42_out);
  and and_15 (ALUASrc, op0, op1, op2, op3, not_43_out, op5, op6);
  and and_16 (ALUBSrc0, op0, op1, op2, op3, not_44_out, op5, op6);
  and and_17 (ExtOP2, op0, op1, op2, op3, not_78_out, op5, op6);
  or or_1 (RegWr, and_4_out, and_5_out, and_6_out);
  and and_18 (MemWr, op0, op1, not_17_out, not_18_out, not_19_out, op5, not_20_out, not_21_out, fn1, not_22_out);
  or or_2 (ALUctr0, and_7_out, and_8_out);
  or or_3 (ALUctr1, and_9_out, and_10_out);
  or or_4 (ALUctr2, and_11_out, and_12_out);
  or or_5 (ALUctr3, and_13_out, and_14_out);
  and and_19 (and_19_out, op0, op1, not_45_out, not_46_out, not_47_out, not_48_out, not_49_out, fn1, not_50_out);
  or or_6 (ALUBSrc1, and_19_out, and_20_out, and_21_out);
  and and_20 (and_20_out, op0, op1, not_51_out, not_52_out, op4, not_53_out, not_54_out, not_55_out, fn1, fn2);
  and and_21 (and_21_out, op0, op1, op2, not_56_out, op4, op5, not_57_out);
  and and_22 (and_22_out, op0, op1, not_58_out, not_59_out, not_60_out, op5, op6, not_61_out, not_62_out, not_63_out);
  or or_7 (ExtOP0, and_22_out, and_23_out);
  and and_23 (and_23_out, op0, op1, op2, not_64_out, op4, op5, not_65_out);
  and and_24 (and_24_out, op0, op1, not_66_out, not_67_out, not_68_out, op5, not_69_out, not_70_out, fn1, not_71_out);
  or or_8 (ExtOP1, and_24_out, and_25_out);
  and and_25 (and_25_out, op0, op1, not_72_out, not_73_out, not_74_out, op5, op6, not_75_out, not_76_out, not_77_out);

  // Notes on the sheet:
  //   op1: pull=down
  //   fn2: pull=down
  //   op3: pull=down
  //   op0: pull=down
  //   op5: pull=down
  //   fn1: pull=down
  //   fn0: pull=down
  //   op4: pull=down
  //   op2: pull=down
  //   op6: pull=down
endmodule
