// Logisim project exp3-1.circ as structural Verilog: 4 circuits, main circuit main
module main (
  output D,
  output EN,
  output CLK,
  output Q,
  output QN,
  output halt
);

  wire clock_1_out;
  wire [2:2] counter_1_q;

  Counter #(.width(3), .max('h7), .behavior("old")) counter_1 (
    .Q({counter_1_q[2], D, CLK}), .carry(halt), .clk(clock_1_out));  // open: load, D, count, clr, preset
  Clock clock_1 (.out(clock_1_out));
  D_Flip_Flop d_flip_flop_1 (.D(D), .EN(1'b1), .CLK(CLK), .Q(Q), .QN(QN));
  LED led_1 (.in(Q));
  LED led_2 (.in(QN));

  assign EN = 1'b1;

  // Notes on the sheet:
  //   顶层模块与自制子模块连接部分
  //   本地Logisim验证区域
  //   按Control+K触发执行，再次按Control+K暂停触发
endmodule

// D锁存器
module D_Latch (
  input  D,
  input  C,
  output Q,
  output QN
);

  wire nand_1_out, nand_2_out, not_1_out;

  not not_1 (not_1_out, D);
  nand nand_1 (nand_1_out, D, C);
  nand nand_2 (nand_2_out, C, not_1_out);
  or or_1 (Q, ~nand_1_out, ~QN);  // OR_Gate
  or or_2 (QN, ~Q, ~nand_2_out);  // OR_Gate

  // Notes on the sheet:
  //   D锁存器子模块实现区域
endmodule

// D触发器
module D_Flip_Flop (
  input  D,
  input  EN,
  input  CLK,
  output Q,
  output QN
);

  wire and_1_out, and_2_out, or_1_out;

  and and_1 (and_1_out, D, EN);
  and and_2 (and_2_out, ~EN, Q);  // AND_Gate
  or or_1 (or_1_out, and_1_out, and_2_out);
  D_Trigger d_trigger_1 (.D(or_1_out), .CLK(CLK), .Q(Q), .QN(QN));

  // Notes on the sheet:
  //   D触发器子模块实现区域
endmodule

module D_Trigger (
  input  D,
  input  CLK,
  output Q,
  output QN
);

  wire d_latch_1_q, not_1_out, not_2_out;

  not not_1 (not_1_out, CLK);
  D_Latch d_latch_1 (.D(D), .C(not_1_out), .Q(d_latch_1_q));  // open: QN
  not not_2 (not_2_out, not_1_out);
  D_Latch d_latch_2 (.D(d_latch_1_q), .C(not_2_out), .Q(Q), .QN(QN));

  // Notes on the sheet:
  //   D触发器子模块实现区域
endmodule
