// Logisim project exp3-3.circ as structural Verilog: 2 circuits, main circuit main
module main (
  output CLK,
  output CLR,
  output LIN,
  output RIN,
  output S1,
  output S0,
  output A,
  output B,
  output C,
  output D,
  output QA,
  output QB,
  output QC,
  output QD,
  output halt
);

  wire [3:0] bit_extender_1_out;
  wire [4:0] counter_1_q;
  wire [15:9] rom_1_data;

  Clock clock_1 (.out(CLK));
  Counter #(.width(5), .max('h1f), .behavior("old")) counter_1 (
    .Q(counter_1_q), .carry(halt), .clk(CLK));  // open: load, D, count, clr, preset
  Bit_Extender #(.in_width(5), .out_width(4), .\type ("zero")) bit_extender_1 (
    .in(counter_1_q), .out(bit_extender_1_out));
  ROM #(.addrWidth(4), .dataWidth(16), .Select("low")) rom_1 (
    .addr(bit_extender_1_out), .data({rom_1_data, CLR, LIN, RIN, S1, S0, A, B, C, D}));
  // Digital_Oscilloscope #(.nState(5), .frontlines("both")) digital_oscilloscope_1: pin names not known; wires that end beside it: CLK, QA, QB, QC, QD
  \_4位移位寄存器  \u_4位移位寄存器_1  (
    .CLK(CLK), .CLR(CLR), .S1(S1), .D(D), .LIN(LIN), .RIN(RIN), .QA(QA), .QB(QB), .QC(QC), .QD(QD), .A(A),
    .B(B), .C(C), .S0(S0));

  // Other names for the same wires on the sheet: A_t = QA; B_t = QB; C_t = QC; D_t = QD

  // Notes on the sheet:
  //   contents of rom_1 (hex, n*v repeats v):
  //   100 35 5f 50 55 5a 90 1f 15f 3a af a0 a5 aa 60 2f
  //   顶层模块与自制子模块连接部分
  //   本地Logisim验证区域
  //   按Control+K触发执行，再次按Control+K暂停触发
endmodule

module \_4位移位寄存器  (
  input  CLK,
  input  CLR,
  input  LIN,
  input  RIN,
  input  S1,
  input  S0,
  input  D,
  input  C,
  input  B,
  input  A,
  output QD,
  output QC,
  output QB,
  output QA
);

  wire _00_2_out, _00_3_out, _00_4_out, _00_out, _01_2_out, _01_3_out, _01_4_out, _01_out, _10_2_out,
       _10_3_out, _10_4_out, _10_out, _11_2_out, _11_3_out, _11_4_out, _11_out, not_1_out, not_2_out,
       not_3_out, not_4_out, not_5_out, not_6_out, or_1_out, or_2_out, or_3_out, or_4_out;

  not not_1 (not_1_out, CLK);
  not not_2 (not_2_out, CLR);
  not not_3 (not_3_out, not_4_out);
  not not_4 (not_4_out, S1);
  not not_5 (not_5_out, S0);
  not not_6 (not_6_out, not_5_out);
  and _10 (_10_out, not_2_out, LIN, not_3_out, not_5_out);
  and _00 (_00_out, not_2_out, QD, not_4_out, not_5_out);
  and _11 (_11_out, not_2_out, D, not_3_out, not_6_out);
  and _01 (_01_out, not_2_out, QC, not_4_out, not_6_out);
  and _10_2 (_10_2_out, not_2_out, QD, not_3_out, not_5_out);
  and _00_2 (_00_2_out, not_2_out, QC, not_4_out, not_5_out);
  and _11_2 (_11_2_out, not_2_out, C, not_3_out, not_6_out);
  and _01_2 (_01_2_out, not_2_out, QB, not_4_out, not_6_out);
  and _10_3 (_10_3_out, not_2_out, QC, not_3_out, not_5_out);
  and _00_3 (_00_3_out, not_2_out, QB, not_4_out, not_5_out);
  and _11_3 (_11_3_out, not_2_out, B, not_3_out, not_6_out);
  and _01_3 (_01_3_out, not_2_out, QA, not_4_out, not_6_out);
  and _10_4 (_10_4_out, not_2_out, QB, not_3_out, not_5_out);
  and _00_4 (_00_4_out, not_2_out, QA, not_4_out, not_5_out);
  and _11_4 (_11_4_out, not_2_out, A, not_3_out, not_6_out);
  and _01_4 (_01_4_out, not_2_out, RIN, not_4_out, not_6_out);
  or or_1 (or_1_out, _10_out, _00_out, _11_out, _01_out);
  or or_2 (or_2_out, _10_2_out, _00_2_out, _11_2_out, _01_2_out);
  or or_3 (or_3_out, _10_3_out, _00_3_out, _11_3_out, _01_3_out);
  or or_4 (or_4_out, _10_4_out, _00_4_out, _11_4_out, _01_4_out);
  D_Flip_Flop d_ff_1 (.clk(not_1_out), .D(or_1_out), .Q(QD));  // open: Qn, preset, reset
  D_Flip_Flop d_ff_2 (.clk(not_1_out), .D(or_2_out), .Q(QC));  // open: Qn, preset, reset
  D_Flip_Flop d_ff_3 (.clk(not_1_out), .D(or_3_out), .Q(QB));  // open: Qn, preset, reset
  D_Flip_Flop d_ff_4 (.clk(not_1_out), .D(or_4_out), .Q(QA));  // open: Qn, preset, reset

  // Notes on the sheet:
  //   4位移位寄存器子模块实现区域
endmodule
