// Logisim project exp5-1.circ as structural Verilog: 2 circuits, main circuit main
module main (
  output [11:0] Addr,
  output [31:0] DataOut,
  output halt
);

  wire clk, \RAM测试写入使能_data ;
  wire [4:0] counter_1_q;
  wire [31:0] DataIn;

  Clock clock_1 (.out(clk));
  Counter #(.width(5), .max('h1f), .trigger("falling")) counter_1 (
    .Q(counter_1_q), .carry(halt), .clk(clk));  // open: load, D, count, clr, preset, down
  Hex_Digit_Display hex_digit_display_1 (.value(Addr[7:4]));  // open: dp
  Hex_Digit_Display hex_digit_display_2 (.value(Addr[11:8]));  // open: dp
  ROM #(.addrWidth(5), .dataWidth(12), .Select("low")) \RAM测试地址取值  (.addr(counter_1_q), .data(Addr));
  ROM #(.addrWidth(5), .dataWidth(32), .Select("low")) \RAM测试写入数据  (.addr(counter_1_q), .data(DataIn));
  ROM #(.addrWidth(5), .dataWidth(1), .Select("low")) \RAM测试写入使能  (.addr(counter_1_q), .data(\RAM测试写入使能_data ));
  Hex_Digit_Display hex_digit_display_3 (.value(Addr[3:0]));  // open: dp
  Hex_Digit_Display hex_digit_display_4 (.value(DataOut[27:24]));  // open: dp
  Hex_Digit_Display hex_digit_display_5 (.value(DataOut[31:28]));  // open: dp
  // Probe on DataIn
  \RAM存储  \ram存储_1  (.Addr(Addr), .DataIn(DataIn), .WriteEn(\RAM测试写入使能_data ), .CLK(clk), .DataOut(DataOut));
  Hex_Digit_Display hex_digit_display_6 (.value(DataOut[23:20]));  // open: dp
  Hex_Digit_Display hex_digit_display_7 (.value(DataOut[19:16]));  // open: dp
  Hex_Digit_Display hex_digit_display_8 (.value(DataIn[31:28]));  // open: dp
  Hex_Digit_Display hex_digit_display_9 (.value(DataIn[27:24]));  // open: dp
  Hex_Digit_Display hex_digit_display_10 (.value(DataOut[15:12]));  // open: dp
  Hex_Digit_Display hex_digit_display_11 (.value(DataOut[11:8]));  // open: dp
  Hex_Digit_Display hex_digit_display_12 (.value(DataIn[23:20]));  // open: dp
  Hex_Digit_Display hex_digit_display_13 (.value(DataIn[19:16]));  // open: dp
  Hex_Digit_Display hex_digit_display_14 (.value(DataOut[7:4]));  // open: dp
  Hex_Digit_Display hex_digit_display_15 (.value(DataOut[3:0]));  // open: dp
  Hex_Digit_Display hex_digit_display_16 (.value(DataIn[11:8]));  // open: dp
  Hex_Digit_Display hex_digit_display_17 (.value(DataIn[15:12]));  // open: dp
  Hex_Digit_Display hex_digit_display_18 (.value(DataIn[3:0]));  // open: dp
  Hex_Digit_Display hex_digit_display_19 (.value(DataIn[7:4]));  // open: dp

  // Notes on the sheet:
  //   RAM测试地址
  //   RAM测试读取数据
  //   contents of RAM测试地址取值 (hex, n*v repeats v):
  //   0 11 22 33 44 55 66 77 88 99 aa bb cc dd ee ff 0 11 22 33 44 55 66 77 88 99 aa bb cc dd ee ff
  //   contents of RAM测试写入数据 (hex, n*v repeats v):
  //   abcdef00 bcdef001 cdef0012 def00123 ef001234 f0012345 123456 1234567 12345678 23456789 3456789a
  //   456789ab 56789abc 6789abcd 789abcde 89abcdef
  //   contents of RAM测试写入使能 (hex, n*v repeats v):
  //   16*1
  //   RAM测试写入数据
  //   顶层模块与自制子模块连接部分
  //   本地Logisim验证区域
  //   按Control+K触发执行，再次按Control+K暂停触发
endmodule

// 32-bit RAM
module \RAM存储  (
  input  CLK,
  input  [11:0] Addr,
  input  [31:0] DataIn,
  input  WriteEn,
  output [31:0] DataOut
);

  RAM #(.addrWidth(12), .dataWidth(32), .bus("separate"), .Select("low")) ram_1 (
    .addr(Addr), .din(DataIn), .data(DataOut), .str(WriteEn), .clk(CLK));  // open: sel, ld, clr

  // Notes on the sheet:
  //   RAM存储和读取子模块实现区域
endmodule
