// Logisim project exp5-2-back.circ as structural Verilog: 5 circuits, main circuit main
module main (
  output [4:0] rd,
  output [4:0] rs1,
  output [4:0] rs2,
  output [6:0] funct7,
  output Branch,
  output Jump,
  output ALUAsrc,
  output [1:0] ALUBsrc,
  output [3:0] ALUctr,
  output MemtoReg,
  output RegWr,
  output MemWr,
  output halt,
  output [2:0] ExtOp
);

  wire clk;
  wire [2:0] \指令测试_1_funct3 ;
  wire [6:0] \指令测试_1_opcode ;
  wire [9:0] Addr;
  wire [11:0] bit_extender_1_out;
  wire [31:0] Instr;

  Clock clock_1 (.out(clk));
  Counter #(.width(4), .max('hf), .trigger("falling")) counter_1 (
    .carry(halt), .clk(clk));  // open: load, D, count, Q, clr, preset, down
  \指令测试  \u_指令测试_1  (
    .CLK(clk), .Jump(Jump), .Branch(Branch), .Zero(1'b1), .opcode(\指令测试_1_opcode ), .rd(rd),
    .funct3(\指令测试_1_funct3 ), .rs1(rs1), .rs2(rs2), .funct7(funct7), .ExtOp(ExtOp), .instr(Instr),
    .instr_addr(Addr));  // open: imm
  assign bit_extender_1_out = {{2{1'b0}}, Addr};  // Bit_Extender bit_extender_1
  // 控制器 控制器_1: pin names not known; wires that end beside it: \指令测试_1_opcode [6], \指令测试_1_opcode [5], Jump, \指令测试_1_opcode [4], \指令测试_1_opcode [3], ALUAsrc, \指令测试_1_opcode [2], \指令测试_1_opcode [1], ALUBsrc[1], \指令测试_1_opcode [0], ALUBsrc[0], ALUctr[3], ALUctr[2], ALUctr[1], ALUctr[0], MemtoReg, \指令测试_1_funct3 [2], RegWr, \指令测试_1_funct3 [1], \指令测试_1_funct3 [0], MemWr, ExtOp[2], ExtOp[1], ExtOp[0], Branch
  Hex_Digit_Display hex_digit_display_1 (.value(Instr[27:24]));  // open: dp
  Hex_Digit_Display hex_digit_display_2 (.value(Instr[31:28]));  // open: dp
  Hex_Digit_Display hex_digit_display_3 (.value(Instr[19:16]));  // open: dp
  Hex_Digit_Display hex_digit_display_4 (.value(Instr[23:20]));  // open: dp
  Hex_Digit_Display hex_digit_display_5 (.value(Instr[15:12]));  // open: dp
  Hex_Digit_Display hex_digit_display_6 (.value(Instr[11:8]));  // open: dp
  Hex_Digit_Display hex_digit_display_7 (.value(bit_extender_1_out[11:8]));  // open: dp
  Hex_Digit_Display hex_digit_display_8 (.value(Instr[7:4]));  // open: dp
  Hex_Digit_Display hex_digit_display_9 (.value(Instr[3:0]));  // open: dp
  Hex_Digit_Display hex_digit_display_10 (.value(bit_extender_1_out[3:0]));  // open: dp
  Hex_Digit_Display hex_digit_display_11 (.value(bit_extender_1_out[7:4]));  // open: dp

  // Notes on the sheet:
  //   当前执行指令原码
  //   下条指令读取地址
  //   顶层模块与自制子模块连接部分
  //   本地Logisim验证区域
  //   按Control+K触发执行，再次按Control+K暂停触发
endmodule

module \指令存储器  (
  input  [9:0] Addr,
  output [31:0] Instr
);

  ROM #(.addrWidth(10), .dataWidth(32), .Select("low")) rom_1 (.addr(Addr), .data(Instr));

  // Notes on the sheet:
  //   指令存储器（ROM）子模块实现区域
  //   contents of rom_1 (hex, n*v repeats v):
  //   a004b3 20af33 20bf33 f00ef13 412483 8137 912223 7ea500e3 0 20 ffffffbf 33 f 0 ffffffef 13 0 41 24
  //   ffffff83 0 0 ffffff81 37 0 ffffff91 22 23 7e ffffffa5 0 ffffffe3 991*0 818ff56f
endmodule

module \立即数扩展器件  (
  input  [31:0] Instr,
  input  [2:0] ExtOp,
  output [31:0] Imm
);

  wire [11:0] bit_extender_4_out;
  wire [19:0] bit_extender_1_out, bit_extender_2_out, bit_extender_3_out;

  assign bit_extender_1_out = {{19{1'b0}}, Instr[31]};  // Bit_Extender bit_extender_1
  assign bit_extender_2_out = {{19{1'b0}}, Instr[31]};  // Bit_Extender bit_extender_2
  assign bit_extender_3_out = {{19{1'b0}}, Instr[31]};  // Bit_Extender bit_extender_3
  assign bit_extender_4_out = {{11{1'b0}}, Instr[31]};  // Bit_Extender bit_extender_4
  Multiplexer #(.select(3), .width(32), .enable("false")) multiplexer_1 (
    .in0({bit_extender_1_out, Instr[31:20]}), .in1({Instr[31:12], {12{1'b0}}}),
    .in2({bit_extender_2_out, Instr[31:25], Instr[11:7]}),
    .in3({bit_extender_3_out, Instr[7], Instr[30:25], Instr[11:8], 1'b0}),
    .in4({bit_extender_4_out, Instr[19:12], Instr[20], Instr[30:21], 1'b0}), .in5({32{1'b0}}),
    .in6({32{1'b0}}), .in7({32{1'b0}}), .out(Imm), .sel(ExtOp));

  // Notes on the sheet:
  //   立即数扩展器件子模块实现区域
endmodule

module \控制器  (
  input  op0,
  input  op1,
  input  op2,
  input  op3,
  input  op4,
  input  op5,
  input  op6,
  input  fn0,
  input  fn1,
  input  fn2,
  output Branch,
  output Jump,
  output MemtoReg,
  output RegWr,
  output MemWr,
  output ALUctr0,
  output ALUctr1,
  output ALUctr2,
  output ALUctr3,
  output ALUASrc,
  output ALUBSrc0,
  output ALUBSrc1,
  output ExtOP0,
  output ExtOP1,
  output ExtOP2
);


  // Notes on the sheet:
  //   op3: pull=down
  //   op5: pull=down
  //   op6: pull=down
  //   op2: pull=down
  //   fn1: pull=down
  //   op1: pull=down
  //   op4: pull=down
  //   fn2: pull=down
  //   op0: pull=down
  //   fn0: pull=down
endmodule

module \指令测试  (
  input  CLK,
  input  Jump,
  input  Branch,
  input  Zero,
  input  [2:0] ExtOp,
  output [9:0] instr_addr,
  output [31:0] instr,
  output [6:0] opcode,
  output [4:0] rd,
  output [2:0] funct3,
  output [4:0] rs1,
  output [4:0] rs2,
  output [6:0] funct7,
  output [31:0] imm
);

  wire and_1_out, or_1_out;
  wire [31:0] adder_1_out, multiplexer_1_out, PC_q;

  Register #(.width(32), .Select("low")) PC (
    .D(adder_1_out), .Q({PC_q[31:12], instr_addr, PC_q[1:0]}), .clk(CLK));  // open: en, clr
  or or_1 (or_1_out, Jump, and_1_out);
  and and_1 (and_1_out, Branch, Zero);
  Multiplexer #(.width(32), .enable("false")) multiplexer_1 (
    .in0(32'h4), .in1(imm), .out(multiplexer_1_out), .sel(or_1_out));
  \立即数扩展器件  \u_立即数扩展器件_1  (.Instr({funct7, instr[24:15], funct3, instr[11:0]}), .ExtOp(ExtOp), .Imm(imm));
  Adder #(.width(32)) adder_1 (
    .a({PC_q[31:12], instr_addr, PC_q[1:0]}), .b(multiplexer_1_out), .out(adder_1_out));  // open: cin, cout
  \指令存储器  \u_指令存储器_1  (.Addr(instr_addr), .Instr({funct7, instr[24:15], funct3, instr[11:0]}));

  assign {instr[31:25], instr[14:12]} = {funct7, funct3};
  assign opcode = instr[6:0];
  assign rd = instr[11:7];
  assign rs1 = instr[19:15];
  assign rs2 = instr[24:20];

  // Notes on the sheet:
  //   指令解析测试子模块实现区域
endmodule
